# Fritzing sketch diagram (saved by Fritzing 0.9.9b)
breadboards: 1

parts:
  U1 = NodeMCU V1.0
  Mod1 = KY-022 Infrared Receiver Module [package="Breakout board"]
  Mod2 = KY-005 Infrared Transmitter Module [package="Breakout board"]
  LED1 = smd LED [color="Red (633nm)" package="1206 [SMD]"]
  LED2 = smd LED [color="Blue (430nm)" package="1206 [SMD]"]
  R1 = Resistor [tolerance=±5% resistance=330 package="0402 [SMD]"]
  R2 = Resistor [tolerance=±5% resistance=330 package="0402 [SMD]"]
  S1 = Pushbutton [package="[THT]"]

nets:
  N1: U1.D2, Mod1.S
  N2: U1.D4, LED1.anode
  VIN: U1.3V3, Mod1.Vin, Mod2.Vin
  N3: U1.GND, Mod1.-, Mod2.-, R1.Pin_0, R2.Pin_0, S1.Pin_3, S1.Pin_4
  N4: U1.D5, S1.Pin_1, S1.Pin_2
  N5: U1.D6, Mod2.S
  N6: U1.D7, LED2.anode
  N7: LED1.cathode, R1.Pin_1
  N8: LED2.cathode, R2.Pin_1

custom parts:
  NodeMCU V1.0: ESP8266 based NodeMCU
  KY-022 Infrared Receiver Module: KY-022 IR receiver module, reacts to 38kHz infrared light.
  KY-005 Infrared Transmitter Module: Arduino IR Transmitter Module Keyes KY-005, emits infrared light at 38KHz.
